// Digital circuit 32位计算机.dig as structural Verilog
module \_32位计算机  (
  input  Clock,
  output [31:0] SP,
  output [3:0] STATE,
  output [7:0] IR,
  output [31:0] PC,
  output [31:0] FP
);

  wire add_1_c_o, and_3_out, and_4_out, and_5_out, and_6_out, and_7_out, and_8_out, and_9_out, and_10_out,
       and_11_out, and_12_out, and_13_out, and_14_out, and_15_out, and_16_out, AV_Keyboard, AV_Telnet,
       clock_t, CLR_IE, comparator_1_eq, comparator_2_eq, comparator_3_eq, CS_IVT, CS_KeyBoard, CS_RAM,
       CS_ROM, CS_Stack, CS_Telnet, CS_Terminal, DN_SP, driverinvsel_1_out, END_CYCLE, Flag_c, Flag_n,
       Flag_v, Flag_v_Bus, Flag_z, HALT, INC_PC, INT_REQ, INT_RET, INT_TAKE, LD_FP, LD_IR, LD_MAR, LD_MDREXT,
       LD_MDRINT, LD_PC, LD_RFlags, LD_Rflags_Bus, LD_Rw, LD_SP, multiplexer_3_out, multiplexer_9_out,
       multiplexer_10_out, multiplexer_11_out, multiplexer_12_out, multiplexer_13_out, multiplexer_14_out,
       not_1_out, not_3_out, not_4_out, not_5_out, not_6_out, not_7_out, not_8_out, not_9_out, not_10_out,
       not_11_out, not_12_out, not_13_out, not_14_out, not_15_out, not_16_out, not_17_out, OE, OE_ALU, OE_FP,
       OE_INT_REQ, OE_MDREXT, OE_MDRINT, OE_PC, OE_Ra, OE_Rb, OE_Rflags, OE_SP, or_1_out, or_5_out, or_6_out,
       or_7_out, or_8_out, or_9_out, or_10_out, R_IE_q, SET_IE, Sign_A, Sign_B, Sign_R, SignedCalc,
       sub_1_c_o, UP_SP, WE, xnor_2_out, xor_2_out, xor_3_out, xor_4_out, xor_5_out;
  wire [1:0] priorityencoder_1_num;
  wire [3:0] ADDR_Ra, ADDR_Rb, ADDR_Rw, MODE_ALU;
  wire [5:0] RegFile_db;
  wire [6:6] RegFile_db_2;
  wire [7:0] telnet_1_out;
  wire [15:0] driver_10_out, keyboard_1_d;
  wire [30:0] multiplexer_8_out, RegFile_da;
  wire [30:7] RegFile_db_3;
  wire [31:0] add_1_s, and_1_out, Dec_s, Div_S_q, Div_S_r, Div_U_q, Div_U_r, driver_1_out, Inc_s, INT_ADDR,
       MAR_q, MDR_EXT_q, MDR_INT_q, multiplexer_4_out, multiplexer_6_out, multiplexer_7_out, nand_1_out,
       nor_1_out, not_2_out, or_3_out, Shift_S_out, Shift_U_out, sub_1_s, xnor_1_out, xor_1_out;
  wire [31:16] driver_10_out_2;
  wire [31:20] IR_q;
  wire [32:0] CU_d, multiplexer_1_out;
  wire [32:23] multiplexer_2_out;
  wire [34:0] CU_INT_d;
  wire [63:0] Mul_S_mul, Mul_U_mul, multiplexer_5_out;

  assign {driver_1_out[31:4], Flag_v_Bus, driver_1_out[2:0]} = OE_INT_REQ ? INT_ADDR : 32'bz;  // Driver driver_1
  CounterPreset #(.maxValue(15), .Bits(4)) u_STATE (
    .en(1'b1), .C(clock_t), .dir(1'b0), .in(4'b0000), .ld(1'b0), .clr(END_CYCLE), .out(STATE));  // open: ovf
  Register #(.Bits(32)) u_IR (
    .D({driver_1_out[31:4], Flag_v_Bus, driver_1_out[2:0]}), .C(clock_t), .en(LD_IR),
    .Q({IR_q, ADDR_Ra, ADDR_Rb, ADDR_Rw, IR}));
  assign {driver_1_out[31:4], Flag_v_Bus, driver_1_out[2:0]} = OE_PC ? PC : 32'bz;  // Driver driver_2
  assign {driver_1_out[31:4], Flag_v_Bus, driver_1_out[2:0]} = OE_Rflags ? {{28{1'b0}}, Flag_v, Flag_n, Flag_c, Flag_z} : 32'bz;  // Driver driver_3
  Comparator #(.Bits(8)) u_HALT (.a(IR), .b(8'hf0), .eq(HALT));  // open: gt, lt
  assign {driver_1_out[31:4], Flag_v_Bus, driver_1_out[2:0]} = OE_Ra ? {Sign_A, RegFile_da} : 32'bz;  // Driver driver_4
  RegisterFile #(.AddrBits(4), .Bits(32)) RegFile (
    .Din({driver_1_out[31:4], Flag_v_Bus, driver_1_out[2:0]}), .we(LD_Rw), .Rw(ADDR_Rw), .C(clock_t),
    .Ra(ADDR_Ra), .Rb(ADDR_Rb), .Da({Sign_A, RegFile_da}),
    .Db({Sign_B, RegFile_db_3, RegFile_db_2[6], RegFile_db}));
  assign {driver_1_out[31:4], Flag_v_Bus, driver_1_out[2:0]} = OE_Rb ? {Sign_B, RegFile_db_3, RegFile_db_2[6], RegFile_db} : 32'bz;  // Driver driver_5
  or or_1 (or_1_out, DN_SP, UP_SP);
  CounterPreset #(.Bits(32)) u_SP (
    .en(or_1_out), .C(clock_t), .dir(DN_SP), .in({driver_1_out[31:4], Flag_v_Bus, driver_1_out[2:0]}),
    .ld(LD_SP), .clr(1'b0), .out(SP));  // open: ovf
  assign {driver_1_out[31:4], Flag_v_Bus, driver_1_out[2:0]} = OE_SP ? SP : 32'bz;  // Driver driver_6
  Register #(.Bits(32)) u_FP (.D({driver_1_out[31:4], Flag_v_Bus, driver_1_out[2:0]}), .C(clock_t), .en(LD_FP), .Q(FP));
  assign {driver_1_out[31:4], Flag_v_Bus, driver_1_out[2:0]} = OE_FP ? FP : 32'bz;  // Driver driver_7
  CounterPreset #(.Bits(32), .isProgramCounter("true")) u_PC (
    .en(INC_PC), .C(clock_t), .dir(1'b0), .in({driver_1_out[31:4], Flag_v_Bus, driver_1_out[2:0]}),
    .ld(LD_PC), .clr(1'b0), .out(PC));  // open: ovf
  ROM #(.AddrBits(4), .Bits(35)) CU_INT (.A(STATE), .sel(INT_TAKE), .D(CU_INT_d));
  not not_1 (not_1_out, INT_TAKE);
  assign {driver_1_out[31:4], Flag_v_Bus, driver_1_out[2:0]} = OE_ALU ? {Sign_R, multiplexer_8_out} : 32'bz;  // Driver driver_8
  Comparator #(.Bits(8)) comparator_1 (.a(IR), .b(8'h33), .eq(comparator_1_eq));  // open: gt, lt
  Multiplexer #(.Bits(35)) multiplexer_1 (
    .sel(INT_TAKE), .in_0({35{1'b0}}), .in_1(CU_INT_d), .out({INT_RET, OE_INT_REQ, multiplexer_1_out}));
  ROM #(.AddrBits(12), .isProgramMemory("true"), .Bits(33)) CU (.A({IR, STATE}), .sel(not_1_out), .D(CU_d));
  assign driverinvsel_1_out = ~comparator_1_eq ? and_5_out : 1'bz;  // DriverInvSel driverinvsel_1
  or or_2 (INC_PC, multiplexer_2_out[23], driverinvsel_1_out);
  Add #(.Bits(32)) add_1 (
    .a({Sign_A, RegFile_da}), .b({Sign_B, RegFile_db_3, RegFile_db_2[6], RegFile_db}), .c_i(1'b0),
    .s(add_1_s), .c_o(add_1_c_o));
  Sub #(.Bits(32)) sub_1 (
    .a({Sign_A, RegFile_da}), .b({Sign_B, RegFile_db_3, RegFile_db_2[6], RegFile_db}), .c_i(1'b0),
    .s(sub_1_s), .c_o(sub_1_c_o));
  BarrelShifter #(.Bits(32)) Shift_U (.in({Sign_A, RegFile_da}), .shift(RegFile_db), .out(Shift_U_out));
  assign and_1_out = {Sign_A, RegFile_da} & {Sign_B, RegFile_db_3, RegFile_db_2[6], RegFile_db};  // And and_1, 32 bits wide
  assign nand_1_out = ~({Sign_A, RegFile_da} & {Sign_B, RegFile_db_3, RegFile_db_2[6], RegFile_db});  // NAnd nand_1, 32 bits wide
  assign or_3_out = {Sign_A, RegFile_da} | {Sign_B, RegFile_db_3, RegFile_db_2[6], RegFile_db};  // Or or_3, 32 bits wide
  assign nor_1_out = ~({Sign_A, RegFile_da} | {Sign_B, RegFile_db_3, RegFile_db_2[6], RegFile_db});  // NOr nor_1, 32 bits wide
  assign xor_1_out = {Sign_A, RegFile_da} ^ {Sign_B, RegFile_db_3, RegFile_db_2[6], RegFile_db};  // XOr xor_1, 32 bits wide
  assign xnor_1_out = ~({Sign_A, RegFile_da} ^ {Sign_B, RegFile_db_3, RegFile_db_2[6], RegFile_db});  // XNOr xnor_1, 32 bits wide
  assign not_2_out = ~{Sign_A, RegFile_da};  // Not not_2, 32 bits wide
  Add #(.Bits(32)) Inc (.a({Sign_A, RegFile_da}), .b(32'h1), .c_i(1'b0), .s(Inc_s));  // open: c_o
  Sub #(.Bits(32)) Dec (.a({Sign_A, RegFile_da}), .b(32'h1), .c_i(1'b0), .s(Dec_s));  // open: c_o
  not not_3 (not_3_out, Flag_z);
  Multiplexer #(.Bits(33)) multiplexer_2 (
    .sel(INT_TAKE), .in_0(CU_d), .in_1(multiplexer_1_out),
    .out({multiplexer_2_out[32:31], SignedCalc, MODE_ALU, WE, OE, multiplexer_2_out[23], SET_IE, CLR_IE, OE_ALU, OE_Rflags, OE_Rb, OE_Ra, OE_MDREXT, OE_MDRINT, OE_PC, OE_SP, OE_FP, LD_Rflags_Bus, LD_RFlags, LD_Rw, LD_IR, LD_MDREXT, LD_MDRINT, LD_MAR, LD_PC, LD_SP, LD_FP, UP_SP, DN_SP}));
  and and_2 (clock_t, Clock, not_4_out);
  not not_4 (not_4_out, HALT);
  BarrelShifter #(.Bits(32), .barrelShifterMode("arithmetic"), .barrelSigned("true")) Shift_S (
    .in({Sign_A, RegFile_da}), .shift({RegFile_db_2[6], RegFile_db}), .out(Shift_S_out));
  or or_4 (END_CYCLE, and_5_out, multiplexer_2_out[32]);
  not not_5 (not_5_out, Flag_c);
  not not_6 (not_6_out, Flag_z);
  xor xor_2 (xor_2_out, Flag_n, Flag_v);
  and and_3 (and_3_out, not_3_out, not_7_out);
  not not_7 (not_7_out, xor_2_out);
  Mul #(.Bits(32)) Mul_U (
    .a({Sign_A, RegFile_da}), .b({Sign_B, RegFile_db_3, RegFile_db_2[6], RegFile_db}), .mul(Mul_U_mul));
  Mul #(.Signed("true"), .Bits(32)) Mul_S (
    .a({Sign_A, RegFile_da}), .b({Sign_B, RegFile_db_3, RegFile_db_2[6], RegFile_db}), .mul(Mul_S_mul));
  Div #(.Bits(32)) Div_U (
    .a({Sign_A, RegFile_da}), .b({Sign_B, RegFile_db_3, RegFile_db_2[6], RegFile_db}), .q(Div_U_q),
    .r(Div_U_r));
  Div #(.remainderPositive("false"), .Signed("true"), .Bits(32)) Div_S (
    .a({Sign_A, RegFile_da}), .b({Sign_B, RegFile_db_3, RegFile_db_2[6], RegFile_db}), .q(Div_S_q),
    .r(Div_S_r));
  and and_4 (and_4_out, not_5_out, not_6_out);
  Multiplexer #(.Selector_Bits(4)) multiplexer_3 (
    .sel(IR_q[23:20]), .in_0(1'b0), .in_1(Flag_c), .in_2(Flag_z), .in_3(and_4_out), .in_4(not_8_out),
    .in_5(not_9_out), .in_6(not_10_out), .in_7(Flag_n), .in_8(Flag_v), .in_9(xor_2_out), .in_10(not_11_out),
    .in_11(and_3_out), .in_12(not_12_out), .in_13(1'b0), .in_14(1'b0), .in_15(1'b0), .out(multiplexer_3_out));
  not not_8 (not_8_out, Flag_c);
  not not_9 (not_9_out, Flag_z);
  not not_10 (not_10_out, and_4_out);
  not not_11 (not_11_out, xor_2_out);
  not not_12 (not_12_out, and_3_out);
  Multiplexer #(.Bits(32)) multiplexer_4 (
    .sel(SignedCalc), .in_0(Shift_U_out), .in_1(Shift_S_out), .out(multiplexer_4_out));
  and and_5 (and_5_out, multiplexer_2_out[31], not_13_out);
  not not_13 (not_13_out, multiplexer_3_out);
  Multiplexer #(.Bits(64)) multiplexer_5 (
    .sel(SignedCalc), .in_0(Mul_U_mul), .in_1(Mul_S_mul), .out(multiplexer_5_out));
  Multiplexer #(.Bits(32)) multiplexer_6 (.sel(SignedCalc), .in_0(Div_U_q), .in_1(Div_S_q), .out(multiplexer_6_out));
  RS_FF R_IE (.S(SET_IE), .C(clock_t), .R(CLR_IE), .Q(R_IE_q));  // open: nQ
  Multiplexer #(.Bits(32)) multiplexer_7 (.sel(SignedCalc), .in_0(Div_U_r), .in_1(Div_S_r), .out(multiplexer_7_out));
  assign {driver_1_out[31:4], Flag_v_Bus, driver_1_out[2:0]} = OE_MDRINT ? MDR_INT_q : 32'bz;  // Driver driver_9
  and and_6 (and_6_out, END_CYCLE, INT_REQ, R_IE_q);
  Register #(.Bits(32)) MDR_EXT (
    .D({driver_1_out[31:4], Flag_v_Bus, driver_1_out[2:0]}), .C(clock_t), .en(LD_MDREXT), .Q(MDR_EXT_q));
  RS_FF rs_ff_1 (.S(and_6_out), .C(clock_t), .R(INT_RET), .Q(INT_TAKE));  // open: nQ
  Register #(.Bits(32)) MDR_INT (.D({driver_10_out_2, driver_10_out}), .C(clock_t), .en(LD_MDRINT), .Q(MDR_INT_q));
  assign {driver_10_out_2, driver_10_out} = OE_MDREXT ? MDR_EXT_q : 32'bz;  // Driver driver_10
  Multiplexer #(.Selector_Bits(4), .Bits(32)) multiplexer_8 (
    .sel(MODE_ALU), .in_0(add_1_s), .in_1(sub_1_s), .in_2(multiplexer_5_out[31:0]), .in_3(multiplexer_6_out),
    .in_4(multiplexer_4_out), .in_5(and_1_out), .in_6(nand_1_out), .in_7(or_3_out), .in_8(nor_1_out),
    .in_9(xor_1_out), .in_10(xnor_1_out), .in_11(not_2_out), .in_12(Inc_s), .in_13(Dec_s),
    .in_14(multiplexer_7_out), .in_15({32{1'b0}}), .out({Sign_R, multiplexer_8_out}));
  Register #(.Bits(32)) MAR (
    .D({driver_1_out[31:4], Flag_v_Bus, driver_1_out[2:0]}), .C(clock_t), .en(LD_MAR), .Q(MAR_q));
  xnor xnor_2 (xnor_2_out, Sign_A, Sign_B);
  xor xor_3 (xor_3_out, Sign_A, Sign_B);
  xor xor_4 (xor_4_out, Sign_A, Sign_R);
  xor xor_5 (xor_5_out, Sign_A, Sign_R);
  Comparator #(.Bits(32)) comparator_2 (
    .a({32{1'b0}}), .b({Sign_R, multiplexer_8_out}), .eq(comparator_2_eq));  // open: gt, lt
  Multiplexer multiplexer_9 (.sel(comparator_3_eq), .in_0(add_1_c_o), .in_1(sub_1_c_o), .out(multiplexer_9_out));
  Comparator #(.Bits(4)) comparator_3 (.a(MODE_ALU), .b(4'b0001), .eq(comparator_3_eq));  // open: gt, lt
  and and_7 (and_7_out, xnor_2_out, xor_4_out);
  and and_8 (and_8_out, xor_3_out, xor_5_out);
  Multiplexer multiplexer_10 (
    .sel(not_14_out), .in_0(driver_1_out[1]), .in_1(multiplexer_9_out), .out(multiplexer_10_out));
  not not_14 (not_14_out, LD_Rflags_Bus);
  Multiplexer multiplexer_11 (.sel(not_17_out), .in_0(driver_1_out[2]), .in_1(Sign_R), .out(multiplexer_11_out));
  Multiplexer multiplexer_12 (.sel(not_15_out), .in_0(Flag_v_Bus), .in_1(multiplexer_13_out), .out(multiplexer_12_out));
  Multiplexer multiplexer_13 (.sel(comparator_3_eq), .in_0(and_7_out), .in_1(and_8_out), .out(multiplexer_13_out));
  not not_15 (not_15_out, LD_Rflags_Bus);
  not not_16 (not_16_out, LD_Rflags_Bus);
  Multiplexer multiplexer_14 (
    .sel(not_16_out), .in_0(driver_1_out[0]), .in_1(comparator_2_eq), .out(multiplexer_14_out));
  or or_5 (or_5_out, LD_Rflags_Bus, LD_RFlags);
  or or_6 (or_6_out, LD_Rflags_Bus, LD_RFlags);
  or or_7 (or_7_out, LD_Rflags_Bus, LD_RFlags);
  not not_17 (not_17_out, LD_Rflags_Bus);
  or or_8 (or_8_out, LD_Rflags_Bus, LD_RFlags);
  Decoder #(.Selector_Bits(4)) decoder_1 (
    .sel(MAR_q[27:24]), .out_0(CS_ROM), .out_1(CS_RAM), .out_2(CS_Stack), .out_3(CS_IVT),
    .out_4(CS_KeyBoard), .out_5(CS_Terminal), .out_6(CS_Telnet));  // open: out_7, out_8, out_9, out_10, out_11, out_12, out_13, out_14, out_15
  Register register_1 (.D(multiplexer_14_out), .C(clock_t), .en(or_5_out), .Q(Flag_z));
  Register register_2 (.D(multiplexer_10_out), .C(clock_t), .en(or_6_out), .Q(Flag_c));
  Register register_3 (.D(multiplexer_11_out), .C(clock_t), .en(or_7_out), .Q(Flag_n));
  Register register_4 (.D(multiplexer_12_out), .C(clock_t), .en(or_8_out), .Q(Flag_v));
  and and_9 (and_9_out, CS_Terminal, WE);
  and and_10 (and_10_out, CS_Telnet, WE);
  and and_11 (and_11_out, CS_Telnet, OE);
  or or_9 (or_9_out, WE, OE);
  or or_10 (or_10_out, WE, OE);
  and and_12 (and_12_out, CS_KeyBoard, OE);
  EEPROM #(.AddrBits(24), .Bits(32)) ROM (
    .A(MAR_q[23:0]), .CS(CS_ROM), .WE(1'b0), .OE(OE), .D({driver_10_out_2, driver_10_out}));
  RAMSinglePortSel #(.AddrBits(24), .Bits(32)) RAM (
    .A(MAR_q[23:0]), .CS(and_13_out), .WE(WE), .OE(OE), .D({driver_10_out_2, driver_10_out}));
  and and_13 (and_13_out, CS_RAM, or_9_out);
  RAMSinglePortSel #(.AddrBits(24), .Bits(32)) Stack (
    .A(MAR_q[23:0]), .CS(CS_Stack), .WE(WE), .OE(OE), .D({driver_10_out_2, driver_10_out}));
  RAMSinglePortSel #(.AddrBits(24), .Bits(32)) IVT (
    .A(MAR_q[23:0]), .CS(and_14_out), .WE(WE), .OE(OE), .D({driver_10_out_2, driver_10_out}));
  and and_14 (and_14_out, CS_IVT, or_10_out);
  Keyboard keyboard_1 (.C(clock_t), .en(and_12_out), .D(keyboard_1_d), .av(AV_Keyboard));
  Terminal terminal_1 (.D(driver_10_out), .C(clock_t), .en(and_9_out));
  Telnet #(.port(8081)) telnet_1 (
    .in(driver_10_out[7:0]), .C(clock_t), .wr(and_10_out), .rd(and_11_out), .out(telnet_1_out), .av(AV_Telnet));
  PriorityEncoder #(.Selector_Bits(2)) priorityencoder_1 (
    .in0(1'b0), .in1(AV_Telnet), .in2(AV_Keyboard), .in3(1'b0), .num(priorityencoder_1_num), .any(INT_REQ));
  and and_15 (and_15_out, CS_KeyBoard, OE);
  assign {driver_10_out_2, driver_10_out} = and_15_out ? {{16{1'b0}}, keyboard_1_d} : 32'bz;  // Driver driver_11
  Multiplexer #(.Selector_Bits(2), .Bits(32)) multiplexer_15 (
    .sel(priorityencoder_1_num), .in_0(32'h3000003), .in_1(32'h3000002), .in_2(32'h3000001),
    .in_3(32'h3000000), .out(INT_ADDR));
  and and_16 (and_16_out, CS_Telnet, OE);
  assign {driver_10_out_2, driver_10_out} = and_16_out ? {{24{1'b0}}, telnet_1_out} : 32'bz;  // Driver driver_12

  // Notes on the sheet:
  //   Clock: Hz: 65536
  //   contents of CU_INT (hex, n*v repeats v):
  //   3c202020,3c004080,3e010002,3c002020,3c080080,3e010002,23c000020
  //   ,3d000040,53c008010
  //   ALU
  //   contents of CU (hex, n*v repeats v):
  //   3c004020,3d800040,3c008100,13c000000,12*3c000000,3c004020,3d800040
  //   ,3c008100,13c000000,12*3c000000,3c004020,3d800040,3c008100,13c000000
  //   ,12*3c000000,3c004020,3d800040,3c008100,13c000000,12*3c000000
  //   ,3c004020,3d800040,3c008100,13c000000,12*3c000000,3c004020,3d800040
  //   ,3c008100,13c000000,12*3c000000,3c004020,3d800040,3c008100,13c000000
  //   ,12*3c000000,3c004020,3d800040,3c008100,13c000000,12*3c000000
  //   ,3c004020,3d800040,3c008100,13c000000,12*3c000000,3c004020,3d800040
  //   ,3c008100,13c000000,12*3c000000,3c004020,3d800040,3c008100,13c000000
  //   ,12*3c000000,3c004020,3d800040,3c008100,13c000000,12*3c000000
  //   ,3c004020,3d800040,3c008100,13c000000,12*3c000000,3c004020,3d800040
  //   ,3c008100,13c000000,12*3c000000,3c004020,3d800040,3c008100,13c000000
  //   ,12*3c000000,3c004020,3d800040,3c008100,13c000000,12*3c000000
  //   ,3c004020,3d800040,3c008100,13c020200,12*3c000000,3c004020,3d800040
  //   ,3c008100,3c040020,3d000040,13c008200,10*3c000000,3c004020,3d800040
  //   ,3c008100,3c040020,3c020080,13e010000,10*3c000000,3c004020,3d800040
  //   ,3c008100,3c004020,3d800040,3c008020,3d000040,13c008200,8*3c000000
  //   ,3c004020,3d800040,3c008100,3c004020,3d800040,3c008020,3c020080
  //   ,13e010000,8*3c000000,3c004020,3d800040,3c008100,3c804020,3d000040
  //   ,13c008200,10*3c000000,3c004020,3d800040,3c008100,3c804020,3d000040
  //   ,13c008200,10*3c000000,3c004020,3d800040,3c008100,100020,3d000040
  //   ,13c008200,10*3c000000,3c004020,3d800040,3c008100,13c000000,12*3c000000
  //   ,3c004020,3d800040,3c008100,13c000000,12*3c000000,3c004020,3d800040
  //   ,3c008100,13c000000,12*3c000000,3c004020,3d800040,3c008100,13c000000
  //   ,12*3c000000,3c004020,3d800040,3c008100,13c000000,12*3c000000
  //   ,3c004020,3d800040,3c008100,13c000000,12*3c000000,3c004020,3d800040
  //   ,3c008100,13c000000,12*3c000000,3c004020,3d800040,3c008100,13c000000
  //   ,12*3c000000,3c004020,3d800040,3c008100,100100600,12*3c000000
  //   ,3c004020,3d800040,3c008100,104100600,12*3c000000,3c004020,3d800040
  //   ,3c008100,130100200,12*3c000000,3c004020,3d800040,3c008100,134100200
  //   ,12*3c000000,3c004020,3d800040,3c008100,108100600,12*3c000000
  //   ,3c004020,3d800040,3c008100,10c100600,12*3c000000,3c004020,3d800040
  //   ,3c008100,138100600,12*3c000000,3c004020,3d800040,3c008100,110100600
  //   ,12*3c000000,3c004020,3d800040,3c008100,114100600,12*3c000000
  //   ,3c004020,3d800040,3c008100,118100600,12*3c000000,3c004020,3d800040
  //   ,3c008100,11c100600,12*3c000000,3c004020,3d800040,3c008100,120100600
  //   ,12*3c000000,3c004020,3d800040,3c008100,124100600,12*3c000000
  //   ,3c004020,3d800040,3c008100,128100600,12*3c000000,3c004020,3d800040
  //   ,3c008100,12c100600,12*3c000000,3c004020,3d800040,3c008100,104000400
  //   ,12*3c000000,3c004020,3d800040,3c008100,3c004020,3d800040,13c008010
  //   ,10*3c000000,3c004020,3d800040,3c008100,80000000,3c004020,3d800040
  //   ,13c008010,9*3c000000,3c004020,3d800040,3c008100,13c020010,12*3c000000
  //   ,3c004020,3d800040,3c008100,80000000,13c020010,11*3c000000,3c004020
  //   ,3d800040,3c008100,3c804020,3d000040,3c002020,3c004080,3e010002
  //   ,13c008010,7*3c000000,3c004020,3d800040,3c008100,80000000,3c804020
  //   ,3d000040,3c002020,3c004080,3e010002,13c008010,6*3c000000,3c004020
  //   ,3d800040,3c008100,3c000001,3c002020,3d000040,13c008010,9*3c000000
  //   ,3c004020,3d800040,3c008100,3c804020,3d000040,3c002020,3c004080
  //   ,3e010002,3c002020,3c080080,3e010002,13c008010,4*3c000000,3c004020
  //   ,3d800040,3c008100,80000000,3c804020,3d000040,3c002020,3c004080
  //   ,3e010002,3c002020,3c080080,3e010002,13c008010,3c000000,3c000000,3c000000
  //   ,3c004020,3d800040,3c008100,3c400001,3c002020,3d000040,3c008801
  //   ,3c002020,3d000040,13c008010,6*3c000000,3c004020,3d800040,3c008100
  //   ,13c400000,12*3c000000,3c004020,3d800040,3c008100,13c200000,12*3c000000
  //   ,3c004020,3d800040,3c008100,13c000000,12*3c000000,3c004020,3d800040
  //   ,3c008100,13c000000,12*3c000000,3c004020,3d800040,3c008100,13c000000
  //   ,12*3c000000,3c004020,3d800040,3c008100,13c000000,12*3c000000
  //   ,3c004020,3d800040,3c008100,3c002020,3c020080,13e010002,10*3c000000
  //   ,3c004020,3d800040,3c008100,3c000001,3c002020,3d000040,13c008200
  //   ,9*3c000000,3c004020,3d800040,3c008100,13c020008,12*3c000000,3c004020
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  //   contents of ROM (hex, n*v repeats v):
  //   e15,2000000,e0042,e0048,e43,f15,9,efe20,e0042,e49,f15,5,efe20
  //   ,4e012,e49,f15,4,efe20,5e012,e49,f15,3,efe20,6e012,e49,f15,2,efe20
  //   ,7e012,e49,f15,1,efe20,8e012,e49,9e012,15,3000001,116,22d,10012
  //   ,15,1ffffcb,e49,f15,6,efe20,e012,615,45,60012,15,1ffffcc,b15,6e
  //   ,b0012,15,1ffffcd,a15,74,a0012,15,1ffffce,315,65,30012,15,1ffffcf
  //   ,c15,72,c0012,15,1ffffd0,215,20,20012,15,1ffffd1,d15,69,d0012
  //   ,15,1ffffd2,b0012,15,1ffffd3,a0012,15,1ffffd4,30012,15,1ffffd5
  //   ,115,67,e49,f15,8,efe20,1e012,10012,15,1ffffd6,30012,15,1ffffd7
  //   ,c0012,15,1ffffd8,115,73,10012,e49,f15,7,efe20,1e012,15,1ffffd9
  //   ,20012,15,1ffffda,a0012,15,1ffffdb,515,6f,50012,15,1ffffdc,20012
  //   ,15,1ffffdd,10012,15,1ffffde,50012,15,1ffffdf,c0012,15,1ffffe0
  //   ,a0012,15,1ffffe1,715,2c,70012,15,1ffffe2,20012,15,1ffffe3,50012
  //   ,15,1ffffe4,b0012,15,1ffffe5,30012,15,1ffffe6,20012,15,1ffffe7
  //   ,715,70,70012,15,1ffffe8,30012,15,1ffffe9,c0012,15,1ffffea,20012
  //   ,15,1ffffeb,715,6c,70012,15,1ffffec,d0012,15,1ffffed,b0012,15
  //   ,1ffffee,30012,815,1ffffef,15,2e,8012,815,1fffff0,28012,815,1fffff1
  //   ,68012,615,1fffff2,b6012,615,1fffff3,815,64,86012,615,1fffff4
  //   ,26012,615,1fffff5,915,77,96012,615,1fffff6,d6012,615,1fffff7
  //   ,a6012,615,1fffff8,915,68,96012,615,1fffff9,26012,615,1fffffa
  //   ,915,27,96012,615,1fffffb,415,5d,46012,415,1fffffc,94012,415,1fffffd
  //   ,4012,415,1fffffe,915,a,94012,415,1ffffff,615,0,64012,415,1ffffbf
  //   ,115,53,14012,415,1ffffc0,54012,415,1ffffc1,c4012,415,1ffffc2
  //   ,a4012,415,1ffffc3,d4012,d15,1ffffc4,bd012,b15,1ffffc5,e49,f15
  //   ,8,efd17,db012,b15,1ffffc6,b012,b15,1ffffc7,b012,b15,1ffffc8,b012
  //   ,15,1ffffc9,90012,15,1ffffca,60012,15,1ffffaf,10012,15,1ffffb0
  //   ,50012,15,1ffffb1,c0012,15,1ffffb2,a0012,15,1ffffb3,30012,15,1ffffb4
  //   ,80012,15,1ffffb5,20012,15,1ffffb6,115,76,10012,15,1ffffb7,115
  //   ,61,10012,15,1ffffb8,70012,15,1ffffb9,115,75,10012,15,1ffffba
  //   ,30012,15,1ffffbb,e49,f15,7,efa17,a0012,a15,1ffffbc,15,3a,a012
  //   ,a15,1ffffbd,9a012,a15,1ffffbe,6a012,a15,1ffffad,9a012,a15,1ffffae
  //   ,6a012,a15,1ffffa5,b15,4e,ba012,a15,1ffffa6,1a012,115,1ffffa7
  //   ,a15,6d,a1012,115,1ffffa8,a15,62,a1012,115,1ffffa9,31012,115,1ffffaa
  //   ,c1012,115,1ffffab,21012,115,1ffffac,61012,115,1ffffa2,1012,15
  //   ,1ffffa3,20012,15,1ffffa4,60012,15,1ffffa1,e49,efe20,e012,60012
  //   ,915,1ffffa0,69012,415,1ffff9f,64012,715,1ffff9e,67012,815,1ffff9d
  //   ,68012,515,1fffb9d,115,400,50010,34,3a1,3b,64012,67012,69012,68012
  //   ,e49,f15,7,ef017,60012,65012,e49,f15,6,ef017,34,38a,3a,7011,602f
  //   ,200031,1bf,3b,15,1ffffbf,34,38a,4411,15,2,4002f,900031,1f1,15
  //   ,1,115,0,215,3,40310,30a10,a0321,10b10,10c10,30,1df,b0b20,3b02f
  //   ,200031,1eb,b5d20,d0720,d811,7911,8902f,c00031,1db,9d012,87012
  //   ,c10,30,1db,c102f,200031,1f1,a202f,a00031,1d5,15,1ffffaf,34,38a
  //   ,715,1,4702f,900031,228,15,3d,e49,f15,6,efe20,e012,915,5000000
  //   ,15,3c,e49,f15,7,efe20,e012,30,210,9012,4602f,200031,228,65820
  //   ,8011,34,358,67620,6402f,a00031,20d,87020,8111,11,1002f,e49,f15
  //   ,6,ef017,200031,20c,e49,f15,7,ef017,30,20c,15,1ffffad,34,38a,f0
  //   ,40,10040,20040,30040,40040,50040,60040,70040,80040,90040,a0040
  //   ,b0040,c0040,d0040,e0040,f0040,15,4000000,11,415,1ffff9e,4211
  //   ,115,0,2102f,200031,259,f41,e41,d41,c41,b41,a41,941,841,741,641
  //   ,541,441,341,241,141,41,39,215,ff,2028,215,2c,202f,b00031,26f
  //   ,215,a,202f,200031,26b,215,d,202f,500031,280,34,2cb,30,248,215
  //   ,2d,202f,200031,2b2,215,5d,202f,500031,280,34,2cb,15,1,4012,30
  //   ,248,315,30,3221,415,9,2402f,300031,248,515,1ffff9f,5411,615,3ff
  //   ,4602f,b00031,248,5611,415,1fffb9d,64620,6611,715,a,67624,715
  //   ,1ffff9d,7711,5511,7102f,200031,2a0,30221,54120,62220,21012,115
  //   ,1ffffa0,215,1,21012,115,1ffffa1,1311,32220,21012,115,5000000
  //   ,1012,30,248,15,1ffffa0,11,102f,500031,248,15,1ffff9d,311,3102f
  //   ,500031,248,115,1,10012,15,1ffffa1,311,31120,10012,15,5000000
  //   ,20012,30,248,46,45,e43,f15,6,efe20,e0042,e49,f15,5,efe20,4e012
  //   ,e49,f15,4,efe20,5e012,e49,f15,3,efe20,6e012,e49,f15,2,efe20,7e012
  //   ,e49,f15,1,efe20,8e012,e49,9e012,515,1ffffa0,5011,415,0,402f,200031
  //   ,33a,615,1ffffa1,6011,715,1,702f,900031,308,15,5000000,115,8,40210
  //   ,10012,27220,6311,2302f,900031,302,15,1ffffa5,34,38a,815,1ffff9f
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endmodule
